// Logisim project Guia_0603d.circ as structural Verilog: 1 circuit, main circuit main
module main (
  input  x,
  input  y,
  input  w,
  input  z,
  output out_5
);

  wire and_1_out, and_2_out, and_3_out, and_4_out, and_5_out, not_1_out, not_2_out, not_3_out, not_4_out,
       or_1_out;

  not not_1 (not_1_out, y);
  not not_2 (not_2_out, x);
  not not_3 (not_3_out, w);
  not not_4 (not_4_out, z);
  and and_1 (and_1_out, w, not_4_out);
  and and_2 (and_2_out, y, not_3_out);
  and and_3 (and_3_out, not_4_out, not_2_out);
  and and_4 (and_4_out, y, not_3_out);
  or or_1 (or_1_out, and_1_out, and_2_out);
  and and_5 (and_5_out, and_3_out, and_4_out);
  and and_6 (out_5, or_1_out, and_5_out);
endmodule
